# Fritzing sketch Final1 (saved by Fritzing 0.9.3b)
stripboards: 3

parts:
  Arduino_Micro_(ATMega32U4)_to_PC_USB_Port = Arduino Micro (Rev3)  # not connected
  Volume = Rotary Encoder with Knob
  Treble_Up = Pushbutton [package="[SMD]"]
  Treble_Down = Pushbutton [package="[SMD]"]
  Bass_Up = Pushbutton [package="[SMD]"]
  Bass_Down = Pushbutton [package="[SMD]"]
  CapsLock_LED = LED - 3mm [color="Red (633nm)" package="3 mm [THT]"]
  R1 = Resistor Mini [tolerance=±5% resistance=470 package=THT]
  R2 = Resistor [tolerance=±5% resistance=470 package="0805 [SMD]"]
  R3 = Resistor Mini [tolerance=±5% resistance=470 package=THT]
  R4 = Resistor Mini [tolerance=±5% resistance=470 package=THT]
  R5 = Resistor Mini [tolerance=±5% resistance=470 package=THT]
  Activity_LED = LED - 3mm [color="Orange (620nm)" package="3 mm [THT]"]
  ScrollLock_LED = LED - 3mm [color="Green (565nm)" package="3 mm [THT]"]
  NumLock_LED = LED - 3mm [color="Yellow (574nm)" package="3 mm [THT]"]
  LED_Volume_Up/Down = LED - 3mm [color="Blue (470nm)" package="3 mm [THT]"]

nets:
  N1: Volume.no_name_yet#2, Volume.no_name_yet#4, LED_Volume_Up/Down.cathode
  N2: Treble_Up.Pin_1, Treble_Up.Pin_2
  N3: Treble_Up.Pin_3, Treble_Up.Pin_4, Treble_Down.Pin_3, Treble_Down.Pin_4, Bass_Up.Pin_3, Bass_Up.Pin_4, Bass_Down.Pin_3, Bass_Down.Pin_4, CapsLock_LED.cathode, Activity_LED.cathode, ScrollLock_LED.cathode, NumLock_LED.cathode
  N4: Treble_Down.Pin_1, Treble_Down.Pin_2
  N5: Bass_Up.Pin_1, Bass_Up.Pin_2
  N6: Bass_Down.Pin_1, Bass_Down.Pin_2
  N7: CapsLock_LED.anode, R4.Pin_0
  N8: R1.Pin_1, Activity_LED.anode
  N9: R2.Pin_0, LED_Volume_Up/Down.anode
  N10: R3.Pin_0, ScrollLock_LED.anode
  N11: R5.Pin_0, NumLock_LED.anode

custom parts:
  Rotary Encoder with Knob: Rotary Encoder with 1/4" Shaft and Knob
  Resistor Mini: A generic resistor (0.25W)
